// Logisim project project.circ as structural Verilog: 10 circuits, main circuit main
module main (
  input  [3:0] joystick_x,
  input  [3:0] joystick_y,
  input  set,
  input  stop,
  input  restart,
  input  glider,
  input  lwss,
  input  explosion,
  output [15:0] outrow0,
  output [15:0] outrow1,
  output [15:0] outrow2,
  output [3:0] small_y,
  output [3:0] small_x,
  output [15:0] outrow3,
  output [3:0] big_y,
  output [3:0] big_x,
  output [15:0] outrow4,
  output [15:0] outrow5,
  output [15:0] outrow6,
  output [15:0] outrow7,
  output [15:0] outrow8,
  output [15:0] outrow9,
  output [15:0] outrow10,
  output [15:0] outrow11,
  output [15:0] outrow12,
  output [15:0] outrow13,
  output [15:0] outrow14,
  output [15:0] outrow15
);

  wire cdm8e_1_row0, cdm8e_1_row1, cdm8e_1_row2, cdm8e_1_row3, cdm8e_1_row4, cdm8e_1_row5, cdm8e_1_row6,
       cdm8e_1_row7, cdm8e_1_row8, cdm8e_1_row9, cdm8e_1_row10, cdm8e_1_row11, cdm8e_1_row12, cdm8e_1_row13,
       cdm8e_1_row14, cdm8e_1_row15, clk;
  wire [7:0] cell_x, cell_y, joystick;

  Clock clock_1 (.out(clk));
  // Probe on joystick_x
  // Probe on joystick_y
  // Probe on joystick
  joystick_parse joystick_parse_1 (.in_1(joystick_x), .in_2(joystick_y), .\output (joystick));
  bcd bcd_1 (.\input (cell_y), .big_digit(big_y), .small_digit(small_y));
  cdm8e cdm8e_1 (
    .clk(clk), .joystick(joystick), .cell_x(cell_x), .cell_y(cell_y), .row0(cdm8e_1_row0),
    .row1(cdm8e_1_row1), .row2(cdm8e_1_row2), .row3(cdm8e_1_row3), .row4(cdm8e_1_row4), .row5(cdm8e_1_row5),
    .row6(cdm8e_1_row6), .row7(cdm8e_1_row7), .row8(cdm8e_1_row8), .row9(cdm8e_1_row9),
    .row10(cdm8e_1_row10), .row11(cdm8e_1_row11), .row12(cdm8e_1_row12), .row13(cdm8e_1_row13),
    .row14(cdm8e_1_row14), .row15(cdm8e_1_row15), .set(set), .glider(glider), .lwss(lwss),
    .explosion(explosion));
  bcd bcd_2 (.\input (cell_x), .big_digit(big_x), .small_digit(small_x));
  game game_1 (
    .clk(clk), .outrow0(outrow0), .outrow1(outrow1), .outrow2(outrow2), .outrow3(outrow3), .outrow4(outrow4),
    .outrow5(outrow5), .outrow6(outrow6), .outrow7(outrow7), .outrow8(outrow8), .outrow9(outrow9),
    .outrow10(outrow10), .outrow11(outrow11), .outrow12(outrow12), .outrow13(outrow13), .outrow14(outrow14),
    .outrow15(outrow15), .stop(stop), .set0(cdm8e_1_row0), .set1(cdm8e_1_row1), .set2(cdm8e_1_row2),
    .set3(cdm8e_1_row3), .set4(cdm8e_1_row4), .set5(cdm8e_1_row5), .set6(cdm8e_1_row6), .set8(cdm8e_1_row8),
    .set9(cdm8e_1_row9), .set10(cdm8e_1_row10), .set11(cdm8e_1_row11), .set12(cdm8e_1_row12),
    .set13(cdm8e_1_row13), .set14(cdm8e_1_row14), .set15(cdm8e_1_row15), .set7(cdm8e_1_row7),
    .cell_x(cell_x), .global_set(set), .restart(restart));  // open: cell_out

  // Other names for the same wires on the sheet: explsn = explosion; rstrt = restart
endmodule

// jstk_prs
module joystick_parse (
  input  [3:0] in_1,
  input  [3:0] in_2,
  output [7:0] \output 
);

  Comparator #(.width(4), .mode("unsigned")) comparator_1 (.a(in_1), .b(4'b0101), .lt(\output [0]));  // open: gt, eq
  Comparator #(.width(4), .mode("unsigned")) comparator_2 (.a(in_1), .b(4'b1010), .gt(\output [1]));  // open: eq, lt
  Comparator #(.width(4), .mode("unsigned")) comparator_3 (.a(in_2), .b(4'b0101), .lt(\output [2]));  // open: gt, eq
  Comparator #(.width(4), .mode("unsigned")) comparator_4 (.a(in_2), .b(4'b1010), .gt(\output [3]));  // open: eq, lt

  assign \output [7:4] = 4'b0000;

  // Notes on the sheet:
  //   left
  //   right
  //   up
  //   down
endmodule

module cdm8e (
  input  glider,
  input  lwss,
  input  explosion,
  input  [7:0] joystick,
  input  clk,
  output row0,
  output row8,
  output set,
  output row1,
  output row9,
  output [7:0] cell_x,
  output row2,
  output row10,
  output [7:0] cell_y,
  output row3,
  output row11,
  output row4,
  output row12,
  output row5,
  output row13,
  output row6,
  output row14,
  output row7,
  output row15
);

  wire addr_out, and_3_out, and_4_out, and_5_out, and_6_out, cdm_8_mark5_1_p1, cdm_8_mark5_1_p2,
       cdm_8_mark5_1_p4, cdm_8_mark5_1_p5, cdm_8_mark5_1_p6, cdm_8_mark5_1_p7, cdm_8_mark5_1_p8,
       cdm_8_mark5_1_p9, cell_x_out, cell_y_out, clk_t, code, data, I_O_sel, in_out_prime, joystick_out, mem,
       nand_1_out, not_1_out, not_2_out, RAM, row0_out, row1_out, row2_out, row3_out, row4_out, row5_out,
       row6_out, row7_out, row8_out, row9_out, row10_out, row11_out, row12_out, row13_out, row14_out,
       row15_out, set_out;
  wire [4:0] I_O_adr;
  wire [6:0] controlled_buffer_7_out;
  wire [7:0] cdm_8_mark5_1_p13, cdm_8_mark5_1_p14, controlled_buffer_4_out, controlled_buffer_5_out,
       controlled_buffer_6_out, controlled_buffer_10_out, controlled_buffer_11_out, controlled_buffer_12_out,
       controlled_buffer_13_out, controlled_buffer_14_out, controlled_buffer_15_out,
       controlled_buffer_16_out, controlled_buffer_17_out, controlled_buffer_18_out,
       controlled_buffer_19_out, controlled_buffer_20_out, controlled_buffer_21_out,
       controlled_buffer_22_out, controlled_buffer_23_out, controlled_buffer_24_out,
       controlled_buffer_25_out, I_O_dat, register_3_q;
  wire [15:5] cdm_8_mark5_1_p12;

  // Probe on cdm_8_mark5_1_p1
  // Probe on cdm_8_mark5_1_p2
  and and_1 (I_O_sel, not_1_out, clk_t, data);
  Clock clock_1 (.out(clk_t));
  // Probe on cdm_8_mark5_1_p5
  // Probe on cdm_8_mark5_1_p6
  // Probe on cdm_8_mark5_1_p4
  not not_1 (not_1_out, nand_1_out);
  and and_2 (RAM, nand_1_out, data);
  // Probe on cdm_8_mark5_1_p8
  // Probe on cdm_8_mark5_1_p7
  // CdM_8_mark5 cdm_8_mark5_1: pin names not known; wires that end beside it: cdm_8_mark5_1_p1, cdm_8_mark5_1_p2, clk_t, cdm_8_mark5_1_p4, cdm_8_mark5_1_p5, cdm_8_mark5_1_p6, cdm_8_mark5_1_p7, cdm_8_mark5_1_p8, cdm_8_mark5_1_p9, mem, in_out_prime, {cdm_8_mark5_1_p12, I_O_adr}, cdm_8_mark5_1_p13, cdm_8_mark5_1_p14, in_out_prime
  nand nand_1 (nand_1_out, cdm_8_mark5_1_p12[5], ~cdm_8_mark5_1_p12[6], ~cdm_8_mark5_1_p12[7]);  // NAND_Gate
  Decoder #(.disabled(0)) decoder_1 (.out0(code), .out1(data), .sel(cdm_8_mark5_1_p9), .en(mem));
  assign I_O_dat = not_2_out ? cdm_8_mark5_1_p13 : 8'bz;  // Controlled_Buffer controlled_buffer_1
  not not_2 (not_2_out, in_out_prime);
  assign cdm_8_mark5_1_p14 = in_out_prime ? I_O_dat : 8'bz;  // Controlled_Buffer controlled_buffer_2
  and u_joystick (joystick_out, I_O_sel, I_O_adr[0], ~I_O_adr[1], ~I_O_adr[2], ~I_O_adr[3], ~I_O_adr[4]);  // AND_Gate
  and u_set (set_out, I_O_sel, ~I_O_adr[0], I_O_adr[1], ~I_O_adr[2], ~I_O_adr[3], ~I_O_adr[4]);  // AND_Gate
  and u_cell_x (cell_x_out, I_O_sel, I_O_adr[0], ~I_O_adr[1], I_O_adr[2], ~I_O_adr[3], ~I_O_adr[4]);  // AND_Gate
  and u_cell_y (cell_y_out, I_O_sel, ~I_O_adr[0], I_O_adr[1], I_O_adr[2], ~I_O_adr[3], ~I_O_adr[4]);  // AND_Gate
  and addr (addr_out, I_O_sel, I_O_adr[0], I_O_adr[1], I_O_adr[2], ~I_O_adr[3], ~I_O_adr[4]);  // AND_Gate
  assign I_O_dat = joystick_out ? joystick : 8'bz;  // Controlled_Buffer controlled_buffer_3
  assign controlled_buffer_4_out = addr_out ? I_O_dat : 8'bz;  // Controlled_Buffer controlled_buffer_4
  ROM #(.addrWidth(16)) rom_1 (.addr({cdm_8_mark5_1_p12, I_O_adr}), .data(I_O_dat), .sel(code));
  RAM ram_1 (
    .addr({cdm_8_mark5_1_p12[7:5], I_O_adr}), .data(I_O_dat), .sel(RAM), .clk(clk_t), .ld(in_out_prime));  // open: clr
  and and_3 (and_3_out, ~in_out_prime, cell_x_out);  // AND_Gate
  assign controlled_buffer_5_out = and_3_out ? I_O_dat : 8'bz;  // Controlled_Buffer controlled_buffer_5
  and and_4 (and_4_out, ~in_out_prime, cell_y_out);  // AND_Gate
  assign controlled_buffer_6_out = and_4_out ? I_O_dat : 8'bz;  // Controlled_Buffer controlled_buffer_6
  assign {controlled_buffer_7_out, set} = set_out ? I_O_dat : 8'bz;  // Controlled_Buffer controlled_buffer_7
  Register #(.trigger("high")) register_1 (
    .D(controlled_buffer_5_out), .en(cell_x_out), .Q(cell_x), .clk(cell_x_out));  // open: clr
  Register #(.trigger("high")) register_2 (
    .D(controlled_buffer_6_out), .en(cell_y_out), .Q(cell_y), .clk(cell_y_out));  // open: clr
  // Probe on register_3_q
  Register #(.trigger("high")) register_3 (
    .D(controlled_buffer_4_out), .en(addr_out), .Q(register_3_q), .clk(addr_out));  // open: clr
  and and_5 (and_5_out, cell_x_out, in_out_prime);
  and and_6 (and_6_out, cell_y_out, in_out_prime);
  assign I_O_dat = and_5_out ? cell_x : 8'bz;  // Controlled_Buffer controlled_buffer_8
  assign I_O_dat = and_6_out ? cell_y : 8'bz;  // Controlled_Buffer controlled_buffer_9
  and u_row0 (row0_out, I_O_sel, I_O_adr[0], I_O_adr[1], I_O_adr[2], ~I_O_adr[3], ~I_O_adr[4]);  // AND_Gate
  assign controlled_buffer_10_out = row0_out ? I_O_dat : 8'bz;  // Controlled_Buffer controlled_buffer_10
  and u_row1 (row1_out, I_O_sel, ~I_O_adr[0], ~I_O_adr[1], ~I_O_adr[2], I_O_adr[3], ~I_O_adr[4]);  // AND_Gate
  assign controlled_buffer_11_out = row1_out ? I_O_dat : 8'bz;  // Controlled_Buffer controlled_buffer_11
  and u_row2 (row2_out, I_O_sel, I_O_adr[0], ~I_O_adr[1], ~I_O_adr[2], I_O_adr[3], ~I_O_adr[4]);  // AND_Gate
  assign controlled_buffer_12_out = row2_out ? I_O_dat : 8'bz;  // Controlled_Buffer controlled_buffer_12
  and u_row3 (row3_out, I_O_sel, ~I_O_adr[0], I_O_adr[1], ~I_O_adr[2], I_O_adr[3], ~I_O_adr[4]);  // AND_Gate
  assign controlled_buffer_13_out = row3_out ? I_O_dat : 8'bz;  // Controlled_Buffer controlled_buffer_13
  and u_row4 (row4_out, I_O_sel, I_O_adr[0], I_O_adr[1], ~I_O_adr[2], I_O_adr[3], ~I_O_adr[4]);  // AND_Gate
  assign controlled_buffer_14_out = row4_out ? I_O_dat : 8'bz;  // Controlled_Buffer controlled_buffer_14
  and u_row5 (row5_out, I_O_sel, ~I_O_adr[0], ~I_O_adr[1], I_O_adr[2], I_O_adr[3], ~I_O_adr[4]);  // AND_Gate
  assign controlled_buffer_15_out = row5_out ? I_O_dat : 8'bz;  // Controlled_Buffer controlled_buffer_15
  and u_row6 (row6_out, I_O_sel, I_O_adr[0], ~I_O_adr[1], I_O_adr[2], I_O_adr[3], ~I_O_adr[4]);  // AND_Gate
  assign controlled_buffer_16_out = row6_out ? I_O_dat : 8'bz;  // Controlled_Buffer controlled_buffer_16
  and u_row7 (row7_out, I_O_sel, ~I_O_adr[0], I_O_adr[1], I_O_adr[2], I_O_adr[3], ~I_O_adr[4]);  // AND_Gate
  assign controlled_buffer_17_out = row7_out ? I_O_dat : 8'bz;  // Controlled_Buffer controlled_buffer_17
  Register #(.width(1), .trigger("high")) register_4 (
    .D(controlled_buffer_10_out[0]), .en(row0_out), .Q(row0), .clk(row0_out));  // open: clr
  Register #(.width(1), .trigger("high")) register_5 (
    .D(controlled_buffer_11_out[0]), .en(row1_out), .Q(row1), .clk(row1_out));  // open: clr
  Register #(.width(1), .trigger("high")) register_6 (
    .D(controlled_buffer_12_out[0]), .en(row2_out), .Q(row2), .clk(row2_out));  // open: clr
  Register #(.width(1), .trigger("high")) register_7 (
    .D(controlled_buffer_13_out[0]), .en(row3_out), .Q(row3), .clk(row3_out));  // open: clr
  Register #(.width(1), .trigger("high")) register_8 (
    .D(controlled_buffer_14_out[0]), .en(row4_out), .Q(row4), .clk(row4_out));  // open: clr
  Register #(.width(1), .trigger("high")) register_9 (
    .D(controlled_buffer_15_out[0]), .en(row5_out), .Q(row5), .clk(row5_out));  // open: clr
  Register #(.width(1), .trigger("high")) register_10 (
    .D(controlled_buffer_16_out[0]), .en(row6_out), .Q(row6), .clk(row6_out));  // open: clr
  Register #(.width(1), .trigger("high")) register_11 (
    .D(controlled_buffer_17_out[0]), .en(row7_out), .Q(row7), .clk(row7_out));  // open: clr
  and u_row8 (row8_out, I_O_sel, I_O_adr[0], I_O_adr[1], I_O_adr[2], I_O_adr[3], ~I_O_adr[4]);  // AND_Gate
  and u_row9 (row9_out, I_O_sel, ~I_O_adr[0], ~I_O_adr[1], ~I_O_adr[2], ~I_O_adr[3], I_O_adr[4]);  // AND_Gate
  and u_row10 (row10_out, I_O_sel, I_O_adr[0], ~I_O_adr[1], ~I_O_adr[2], ~I_O_adr[3], I_O_adr[4]);  // AND_Gate
  and u_row11 (row11_out, I_O_sel, ~I_O_adr[0], I_O_adr[1], ~I_O_adr[2], ~I_O_adr[3], I_O_adr[4]);  // AND_Gate
  and u_row12 (row12_out, I_O_sel, I_O_adr[0], I_O_adr[1], ~I_O_adr[2], ~I_O_adr[3], I_O_adr[4]);  // AND_Gate
  and u_row13 (row13_out, I_O_sel, ~I_O_adr[0], ~I_O_adr[1], I_O_adr[2], ~I_O_adr[3], I_O_adr[4]);  // AND_Gate
  and u_row14 (row14_out, I_O_sel, I_O_adr[0], ~I_O_adr[1], I_O_adr[2], ~I_O_adr[3], I_O_adr[4]);  // AND_Gate
  and u_row15 (row15_out, I_O_sel, ~I_O_adr[0], I_O_adr[1], I_O_adr[2], ~I_O_adr[3], I_O_adr[4]);  // AND_Gate
  assign controlled_buffer_18_out = row8_out ? I_O_dat : 8'bz;  // Controlled_Buffer controlled_buffer_18
  assign controlled_buffer_19_out = row9_out ? I_O_dat : 8'bz;  // Controlled_Buffer controlled_buffer_19
  assign controlled_buffer_20_out = row10_out ? I_O_dat : 8'bz;  // Controlled_Buffer controlled_buffer_20
  assign controlled_buffer_21_out = row11_out ? I_O_dat : 8'bz;  // Controlled_Buffer controlled_buffer_21
  assign controlled_buffer_22_out = row12_out ? I_O_dat : 8'bz;  // Controlled_Buffer controlled_buffer_22
  assign controlled_buffer_23_out = row13_out ? I_O_dat : 8'bz;  // Controlled_Buffer controlled_buffer_23
  assign controlled_buffer_24_out = row14_out ? I_O_dat : 8'bz;  // Controlled_Buffer controlled_buffer_24
  assign controlled_buffer_25_out = row15_out ? I_O_dat : 8'bz;  // Controlled_Buffer controlled_buffer_25
  keyboard keyboard_1 (
    .I_O_dat(I_O_dat), .glider(glider), .lwss(lwss), .explosion(explosion), .I_O_adr(I_O_adr), .sel(I_O_sel));
  Register #(.width(1), .trigger("high")) register_12 (
    .D(controlled_buffer_18_out[0]), .en(row8_out), .Q(row8), .clk(row8_out));  // open: clr
  Register #(.width(1), .trigger("high")) register_13 (
    .D(controlled_buffer_19_out[0]), .en(row9_out), .Q(row9), .clk(row9_out));  // open: clr
  Register #(.width(1), .trigger("high")) register_14 (
    .D(controlled_buffer_20_out[0]), .en(row10_out), .Q(row10), .clk(row10_out));  // open: clr
  Register #(.width(1), .trigger("high")) register_15 (
    .D(controlled_buffer_21_out[0]), .en(row11_out), .Q(row11), .clk(row11_out));  // open: clr
  Register #(.width(1), .trigger("high")) register_16 (
    .D(controlled_buffer_22_out[0]), .en(row12_out), .Q(row12), .clk(row12_out));  // open: clr
  Register #(.width(1), .trigger("high")) register_17 (
    .D(controlled_buffer_23_out[0]), .en(row13_out), .Q(row13), .clk(row13_out));  // open: clr
  Register #(.width(1), .trigger("high")) register_18 (
    .D(controlled_buffer_24_out[0]), .en(row14_out), .Q(row14), .clk(row14_out));  // open: clr
  Register #(.width(1), .trigger("high")) register_19 (
    .D(controlled_buffer_25_out[0]), .en(row15_out), .Q(row15), .clk(row15_out));  // open: clr
  // also tied to GND on the sheet: {controlled_buffer_7_out[0], controlled_buffer_7_out[1], controlled_buffer_7_out[2], controlled_buffer_7_out[3], controlled_buffer_7_out[4], controlled_buffer_7_out[5], controlled_buffer_7_out[6]}

  // Other names for the same wires on the sheet: rd_wr_prime = in_out_prime

  // Notes on the sheet:
  //   contents of rom_1 (hex, n*v repeats v):
  //   d0 7 d1 25 a4 0 e4 73 c0 d2 21 ba 92 2f 92 2f d0 2 48 0 e0 b d0 26 b1 8d a1 d6 7b 0 ee f d0 1 48 0
  //   e0 9 d0 26 b1 89 a1 d6 7b 0 d0 2 4c 0 e0 b d0 25 b1 89 a1 d6 7b 0 ee f d0 1 4c 0 e0 9 d0 25 b1 8d a1
  //   d6 7b 0 d1 26 b5 5 e5 4 d3 10 1d d0 23 b0 0 e0 19 d2 27 d3 24 bf 1b 30 ac 16 d3 1 ab d0 22 b3 3f a3
  //   ab d0 23 a3 d3 24 ad 30 35 3a 3f c4 ee 8c d4 d0 23 b1 8d a1 d7
  //   высокий уровень!
endmodule

module displ_module (
  input  [7:0] lo,
  input  set_Lo,
  input  [7:0] hi,
  input  sel_Hi,
  input  [7:0] adr,
  input  sel_adr,
  input  clk,
  output [15:0] _1st_row,
  output [15:0] _2nd_row,
  output [15:0] _3rd_row,
  output [15:0] _4th_row,
  output [15:0] _5th_row,
  output [15:0] _6th_row,
  output [15:0] _7th_row,
  output [15:0] _8th_row,
  output [15:0] _9th_row,
  output [15:0] _10th_row,
  output [15:0] _11th_row,
  output [15:0] _12th_row,
  output [15:0] _13th_row,
  output [15:0] _14th_row,
  output [15:0] _15th_row,
  output [15:0] _16th_row
);

  wire demultiplexer_1_out0, demultiplexer_1_out1, demultiplexer_1_out2, demultiplexer_1_out3,
       demultiplexer_1_out4, demultiplexer_1_out5, demultiplexer_1_out6, demultiplexer_1_out7,
       demultiplexer_1_out8, demultiplexer_1_out9, demultiplexer_1_out10, demultiplexer_1_out11,
       demultiplexer_1_out12, demultiplexer_1_out13, demultiplexer_1_out14, demultiplexer_1_out15;
  wire [7:0] register_1_q, register_2_q, register_3_q;

  Register register_1 (.D(lo), .en(set_Lo), .Q(register_1_q), .clk(clk));  // open: clr
  Register register_2 (.D(hi), .en(sel_Hi), .Q(register_2_q), .clk(clk));  // open: clr
  Demultiplexer #(.select(4), .disabled(0)) demultiplexer_1 (
    .out0(demultiplexer_1_out0), .out1(demultiplexer_1_out1), .out2(demultiplexer_1_out2),
    .out3(demultiplexer_1_out3), .out4(demultiplexer_1_out4), .out5(demultiplexer_1_out5),
    .out6(demultiplexer_1_out6), .out7(demultiplexer_1_out7), .out8(demultiplexer_1_out8),
    .out9(demultiplexer_1_out9), .out10(demultiplexer_1_out10), .out11(demultiplexer_1_out11),
    .out12(demultiplexer_1_out12), .out13(demultiplexer_1_out13), .out14(demultiplexer_1_out14),
    .out15(demultiplexer_1_out15), .in(sel_adr), .sel(register_3_q[3:0]), .en(sel_adr));
  Register register_3 (.D(adr), .en(sel_adr), .Q(register_3_q), .clk(clk));  // open: clr
  // Probe on register_3_q
  Register #(.width(16)) register_4 (
    .D({register_2_q, register_1_q}), .en(demultiplexer_1_out0), .Q(_1st_row), .clk(clk));  // open: clr
  Register #(.width(16)) register_5 (
    .D({register_2_q, register_1_q}), .en(demultiplexer_1_out1), .Q(_2nd_row), .clk(clk));  // open: clr
  Register #(.width(16)) register_6 (
    .D({register_2_q, register_1_q}), .en(demultiplexer_1_out2), .Q(_3rd_row), .clk(clk));  // open: clr
  Register #(.width(16)) register_7 (
    .D({register_2_q, register_1_q}), .en(demultiplexer_1_out3), .Q(_4th_row), .clk(clk));  // open: clr
  Register #(.width(16)) register_8 (
    .D({register_2_q, register_1_q}), .en(demultiplexer_1_out4), .Q(_5th_row), .clk(clk));  // open: clr
  Register #(.width(16)) register_9 (
    .D({register_2_q, register_1_q}), .en(demultiplexer_1_out5), .Q(_6th_row), .clk(clk));  // open: clr
  Register #(.width(16)) register_10 (
    .D({register_2_q, register_1_q}), .en(demultiplexer_1_out6), .Q(_7th_row), .clk(clk));  // open: clr
  Register #(.width(16)) register_11 (
    .D({register_2_q, register_1_q}), .en(demultiplexer_1_out7), .Q(_8th_row), .clk(clk));  // open: clr
  Register #(.width(16)) register_12 (
    .D({register_2_q, register_1_q}), .en(demultiplexer_1_out8), .Q(_9th_row), .clk(clk));  // open: clr
  Register #(.width(16)) register_13 (
    .D({register_2_q, register_1_q}), .en(demultiplexer_1_out9), .Q(_10th_row), .clk(clk));  // open: clr
  Register #(.width(16)) register_14 (
    .D({register_2_q, register_1_q}), .en(demultiplexer_1_out10), .Q(_11th_row), .clk(clk));  // open: clr
  Register #(.width(16)) register_15 (
    .D({register_2_q, register_1_q}), .en(demultiplexer_1_out11), .Q(_12th_row), .clk(clk));  // open: clr
  Register #(.width(16)) register_16 (
    .D({register_2_q, register_1_q}), .en(demultiplexer_1_out12), .Q(_13th_row), .clk(clk));  // open: clr
  Register #(.width(16)) register_17 (
    .D({register_2_q, register_1_q}), .en(demultiplexer_1_out13), .Q(_14th_row), .clk(clk));  // open: clr
  Register #(.width(16)) register_18 (
    .D({register_2_q, register_1_q}), .en(demultiplexer_1_out14), .Q(_15th_row), .clk(clk));  // open: clr
  Register #(.width(16)) register_19 (
    .D({register_2_q, register_1_q}), .en(demultiplexer_1_out15), .Q(_16th_row), .clk(clk));  // open: clr
endmodule

module \cell  (
  input  ul_nb,
  input  up_nb,
  input  ur_nb,
  input  right_nb,
  input  left_nb,
  input  dr_nb,
  input  dl_nb,
  input  down_nb,
  input  set,
  input  clk,
  input  stop,
  input  choose,
  input  restart,
  output exit,
  output exit_2,
  output \output 
);

  wire and_1_out, and_2_out, and_3_out, multiplexer_1_out, multiplexer_2_out, not_1_out, not_2_out,
       not_3_out, not_4_out, or_1_out, or_2_out, pull_resistor_1_node;
  wire [2:0] adder_1_out, adder_2_out, adder_3_out, adder_4_out, adder_5_out, adder_6_out, adder_7_out,
       xnor_1_out, xnor_2_out;

  Adder #(.width(3)) adder_1 (.a({2'b00, ul_nb}), .b({2'b00, up_nb}), .out(adder_1_out));  // open: cin, cout
  Adder #(.width(3)) adder_2 (.a({2'b00, ur_nb}), .b({2'b00, right_nb}), .out(adder_2_out));  // open: cin, cout
  Adder #(.width(3)) adder_3 (.a({2'b00, left_nb}), .b({2'b00, dr_nb}), .out(adder_3_out));  // open: cin, cout
  Adder #(.width(3)) adder_4 (.a({2'b00, dl_nb}), .b({2'b00, down_nb}), .out(adder_4_out));  // open: cin, cout
  not not_1 (not_1_out, set);
  Adder #(.width(3)) adder_5 (.a(adder_1_out), .b(adder_2_out), .out(adder_5_out));  // open: cin, cout
  Adder #(.width(3)) adder_6 (.a(adder_3_out), .b(adder_4_out), .out(adder_6_out));  // open: cin, cout
  and and_1 (and_1_out, not_1_out, not_2_out);
  not not_2 (not_2_out, not_1_out);
  Adder #(.width(3)) adder_7 (.a(adder_5_out), .b(adder_6_out), .out(adder_7_out));  // open: cin, cout
  or or_1 (or_1_out, and_1_out, clk);
  D_Flip_Flop d_ff_1 (.clk(or_1_out), .D(multiplexer_2_out), .Q(exit), .reset(restart));  // open: Qn, preset, en
  assign xnor_1_out = ~(3'b010 ^ adder_7_out);  // XNOR_Gate xnor_1, 3 bits wide
  assign xnor_2_out = ~(adder_7_out ^ 3'b011);  // XNOR_Gate xnor_2, 3 bits wide
  and and_2 (and_2_out, xnor_2_out[0], xnor_2_out[1], xnor_2_out[2]);
  not not_3 (not_3_out, exit);
  Multiplexer #(.enable("false")) multiplexer_1 (.in0(exit), .in1(not_3_out), .out(multiplexer_1_out), .sel(set));
  and and_3 (and_3_out, exit, xnor_1_out[0], xnor_1_out[1], xnor_1_out[2]);
  or or_2 (or_2_out, and_3_out, and_2_out);
  Pull_Resistor #(.pull("X")) pull_resistor_1 (.node(pull_resistor_1_node));
  Multiplexer #(.enable("false")) multiplexer_2 (
    .in0(or_2_out), .in1(multiplexer_1_out), .out(multiplexer_2_out), .sel(stop));
  assign \output  = choose ? pull_resistor_1_node : 1'bz;  // Controlled_Buffer controlled_buffer_1
  not not_4 (not_4_out, choose);
  assign \output  = not_4_out ? exit : 1'bz;  // Controlled_Buffer controlled_buffer_2
  Pull_Resistor pull_resistor_2 (.node(\output ));

  assign exit_2 = exit;

  // Other names for the same wires on the sheet: rstrt = restart
endmodule

module row (
  input  nb1,
  input  nb2,
  input  nb3,
  input  nb4,
  input  nb5,
  input  nb6,
  input  nb7,
  input  nb8,
  input  nb9,
  input  nb10,
  input  nb11,
  input  nb12,
  input  nb13,
  input  nb14,
  input  nb15,
  input  nb16,
  input  nb17,
  input  nb18,
  input  nb19,
  input  nb20,
  input  nb21,
  input  nb22,
  input  nb23,
  input  nb24,
  input  nb25,
  input  nb26,
  input  nb27,
  input  nb28,
  input  nb29,
  input  nb30,
  input  nb31,
  input  nb32,
  input  restart,
  input  clk,
  input  stop,
  input  set,
  input  [7:0] adr,
  input  button,
  output ex1,
  output ex2,
  output ex3,
  output ex4,
  output ex5,
  output ex6,
  output ex7,
  output ex8,
  output ex9,
  output ex10,
  output ex11,
  output ex12,
  output ex13,
  output ex14,
  output ex15,
  output ex16,
  output ex17,
  output ex18,
  output ex19,
  output ex20,
  output ex21,
  output ex22,
  output ex23,
  output ex24,
  output ex25,
  output ex26,
  output ex27,
  output ex28,
  output ex29,
  output ex30,
  output ex31,
  output ex32,
  output [15:0] \output ,
  output cell_out
);

  wire and_1_out, and_2_out, cell_1_exit_2, cell_2_exit_2, cell_3_exit_2, cell_4_exit_2, cell_5_exit_2,
       cell_6_exit_2, cell_7_exit_2, cell_8_exit_2, cell_9_exit_2, cell_10_exit_2, cell_11_exit_2,
       cell_12_exit_2, cell_13_exit_2, cell_14_exit_2, cell_15_exit_2, chos1, chos2, chos3, chos4, chos5,
       chos6, chos7, chos8, chos9, chos10, chos11, chos12, chos13, chos14, chos15, chos16, r_l, set1, set2,
       set3, set4, set5, set6, set7, set8, set9, set10, set11, set12, set13, set14, set15, set16;

  \cell  cell_1 (
    .ul_nb(nb16), .left_nb(r_l), .set(set1), .dl_nb(nb32), .ur_nb(nb2), .right_nb(ex2), .dr_nb(nb18),
    .up_nb(nb1), .down_nb(nb17), .exit(ex1), .exit_2(cell_1_exit_2), .clk(clk), .stop(stop), .choose(chos1),
    .\output (\output [15]), .restart(restart));
  and and_1 (and_1_out, set, button);
  and and_2 (and_2_out, set, stop);
  // Probe on adr
  // Probe on adr
  \cell  cell_2 (
    .ul_nb(nb1), .left_nb(cell_1_exit_2), .set(set2), .dl_nb(nb17), .ur_nb(nb3), .right_nb(ex3),
    .dr_nb(nb19), .up_nb(nb2), .down_nb(nb18), .exit(ex2), .exit_2(cell_2_exit_2), .clk(clk), .stop(stop),
    .choose(chos2), .\output (\output [14]), .restart(restart));
  Demultiplexer #(.select(4), .disabled(0)) demultiplexer_1 (
    .out0(set1), .out1(set2), .out2(set3), .out3(set4), .out4(set5), .out5(set6), .out6(set7), .out7(set8),
    .out8(set9), .out9(set10), .out10(set11), .out11(set12), .out12(set13), .out13(set14), .out14(set15),
    .out15(set16), .in(and_1_out), .sel(adr[3:0]), .en(and_1_out));
  Demultiplexer #(.select(4), .disabled(0)) demultiplexer_2 (
    .out0(chos1), .out1(chos2), .out2(chos3), .out3(chos4), .out4(chos5), .out5(chos6), .out6(chos7),
    .out7(chos8), .out8(chos9), .out9(chos10), .out10(chos11), .out11(chos12), .out12(chos13),
    .out13(chos14), .out14(chos15), .out15(chos16), .in(and_2_out), .sel(adr[3:0]), .en(and_2_out));
  \cell  cell_3 (
    .ul_nb(nb2), .left_nb(cell_2_exit_2), .set(set3), .dl_nb(nb18), .ur_nb(nb4), .right_nb(ex4),
    .dr_nb(nb20), .up_nb(nb3), .down_nb(nb19), .exit(ex3), .exit_2(cell_3_exit_2), .clk(clk), .stop(stop),
    .choose(chos3), .\output (\output [13]), .restart(restart));
  \cell  cell_4 (
    .ul_nb(nb3), .left_nb(cell_3_exit_2), .set(set4), .dl_nb(nb19), .ur_nb(nb5), .right_nb(ex5),
    .dr_nb(nb21), .up_nb(nb4), .down_nb(nb20), .exit(ex4), .exit_2(cell_4_exit_2), .clk(clk), .stop(stop),
    .choose(chos4), .\output (\output [12]), .restart(restart));
  \cell  cell_5 (
    .ul_nb(nb4), .left_nb(cell_4_exit_2), .set(set5), .dl_nb(nb20), .ur_nb(nb6), .right_nb(ex6),
    .dr_nb(nb22), .up_nb(nb5), .down_nb(nb21), .exit(ex5), .exit_2(cell_5_exit_2), .clk(clk), .stop(stop),
    .choose(chos5), .\output (\output [11]), .restart(restart));
  \cell  cell_6 (
    .ul_nb(nb5), .left_nb(cell_5_exit_2), .set(set6), .dl_nb(nb21), .ur_nb(nb7), .right_nb(ex7),
    .dr_nb(nb23), .up_nb(nb6), .down_nb(nb22), .exit(ex6), .exit_2(cell_6_exit_2), .clk(clk), .stop(stop),
    .choose(chos6), .\output (\output [10]), .restart(restart));
  \cell  cell_7 (
    .ul_nb(nb6), .left_nb(cell_6_exit_2), .set(set7), .dl_nb(nb22), .ur_nb(nb8), .right_nb(ex8),
    .dr_nb(nb24), .up_nb(nb7), .down_nb(nb23), .exit(ex7), .exit_2(cell_7_exit_2), .clk(clk), .stop(stop),
    .choose(chos7), .\output (\output [9]), .restart(restart));
  \cell  cell_8 (
    .ul_nb(nb7), .left_nb(cell_7_exit_2), .set(set8), .dl_nb(nb23), .ur_nb(nb9), .right_nb(ex9),
    .dr_nb(nb25), .up_nb(nb8), .down_nb(nb24), .exit(ex8), .exit_2(cell_8_exit_2), .clk(clk), .stop(stop),
    .choose(chos8), .\output (\output [8]), .restart(restart));
  Multiplexer #(.select(4), .enable("false")) multiplexer_1 (
    .in0(\output [15]), .in1(\output [14]), .in2(\output [13]), .in3(\output [12]), .in4(\output [11]),
    .in5(\output [10]), .in6(\output [9]), .in7(\output [8]), .in8(\output [7]), .in9(\output [6]),
    .in10(\output [5]), .in11(\output [4]), .in12(\output [3]), .in13(\output [2]), .in14(\output [1]),
    .in15(\output [0]), .out(cell_out), .sel(adr[3:0]));
  \cell  cell_9 (
    .ul_nb(nb8), .left_nb(cell_8_exit_2), .set(set9), .dl_nb(nb24), .ur_nb(nb10), .right_nb(ex10),
    .dr_nb(nb26), .up_nb(nb9), .down_nb(nb25), .exit(ex9), .exit_2(cell_9_exit_2), .clk(clk), .stop(stop),
    .choose(chos9), .\output (\output [7]), .restart(restart));
  \cell  cell_10 (
    .ul_nb(nb9), .left_nb(cell_9_exit_2), .set(set10), .dl_nb(nb25), .ur_nb(nb11), .right_nb(ex11),
    .dr_nb(nb27), .up_nb(nb10), .down_nb(nb26), .exit(ex10), .exit_2(cell_10_exit_2), .clk(clk), .stop(stop),
    .choose(chos10), .\output (\output [6]), .restart(restart));
  \cell  cell_11 (
    .ul_nb(nb10), .left_nb(cell_10_exit_2), .set(set11), .dl_nb(nb26), .ur_nb(nb12), .right_nb(ex12),
    .dr_nb(nb28), .up_nb(nb11), .down_nb(nb27), .exit(ex11), .exit_2(cell_11_exit_2), .clk(clk), .stop(stop),
    .choose(chos11), .\output (\output [5]), .restart(restart));
  \cell  cell_12 (
    .ul_nb(nb11), .left_nb(cell_11_exit_2), .set(set12), .dl_nb(nb27), .ur_nb(nb13), .right_nb(ex13),
    .dr_nb(nb29), .up_nb(nb12), .down_nb(nb28), .exit(ex12), .exit_2(cell_12_exit_2), .clk(clk), .stop(stop),
    .choose(chos12), .\output (\output [4]), .restart(restart));
  \cell  cell_13 (
    .ul_nb(nb12), .left_nb(cell_12_exit_2), .set(set13), .dl_nb(nb28), .ur_nb(nb14), .right_nb(ex14),
    .dr_nb(nb30), .up_nb(nb13), .down_nb(nb29), .exit(ex13), .exit_2(cell_13_exit_2), .clk(clk), .stop(stop),
    .choose(chos13), .\output (\output [3]), .restart(restart));
  \cell  cell_14 (
    .ul_nb(nb13), .left_nb(cell_13_exit_2), .set(set14), .dl_nb(nb29), .ur_nb(nb15), .right_nb(ex15),
    .dr_nb(nb31), .up_nb(nb14), .down_nb(nb30), .exit(ex14), .exit_2(cell_14_exit_2), .clk(clk), .stop(stop),
    .choose(chos14), .\output (\output [2]), .restart(restart));
  \cell  cell_15 (
    .ul_nb(nb14), .left_nb(cell_14_exit_2), .set(set15), .dl_nb(nb30), .ur_nb(nb16), .right_nb(ex16),
    .dr_nb(nb32), .up_nb(nb15), .down_nb(nb31), .exit(ex15), .exit_2(cell_15_exit_2), .clk(clk), .stop(stop),
    .choose(chos15), .\output (\output [1]), .restart(restart));
  \cell  cell_16 (
    .ul_nb(nb15), .left_nb(cell_15_exit_2), .set(set16), .dl_nb(nb31), .ur_nb(nb1), .right_nb(ex1),
    .dr_nb(nb17), .up_nb(nb16), .down_nb(nb32), .exit(ex16), .exit_2(r_l), .clk(clk), .stop(stop),
    .choose(chos16), .\output (\output [0]), .restart(restart));

  assign ex17 = ex1;
  assign ex18 = ex2;
  assign ex19 = ex3;
  assign ex20 = ex4;
  assign ex21 = ex5;
  assign ex22 = ex6;
  assign ex23 = ex7;
  assign ex24 = ex8;
  assign ex25 = ex9;
  assign ex26 = ex10;
  assign ex27 = ex11;
  assign ex28 = ex12;
  assign ex29 = ex13;
  assign ex30 = ex14;
  assign ex31 = ex15;
  assign ex32 = ex16;

  // Other names for the same wires on the sheet: addr[7:0] = adr; adr_t[3:0] = adr[3:0]; l_r = ex1;
  //   ld_to_rd_nb = nb17; lu_to_ru_nb = nb1; out15 = \output [0]; out14 = \output [1]; out13 = \output [2];
  //   out12 = \output [3]; out11 = \output [4]; out10 = \output [5]; out9 = \output [6]; out8 = \output [7];
  //   out7 = \output [8]; out6 = \output [9]; out5 = \output [10]; out4 = \output [11]; out3 = \output [12];
  //   out2 = \output [13]; out1 = \output [14]; out0 = \output [15]; rd_to_ld_nb = nb32; rstrt = restart;
  //   ru_to_lu_nb = nb16
endmodule

module game (
  input  set0,
  input  set1,
  input  set2,
  input  set3,
  input  set4,
  input  set5,
  input  set6,
  input  set7,
  input  set8,
  input  clk,
  input  set9,
  input  set10,
  input  stop,
  input  set11,
  input  [7:0] cell_x,
  input  set12,
  input  set13,
  input  global_set,
  input  restart,
  input  set14,
  input  set15,
  output [15:0] outrow0,
  output [15:0] outrow1,
  output [15:0] outrow2,
  output cell_out,
  output [15:0] outrow3,
  output [15:0] outrow4,
  output [15:0] outrow5,
  output [15:0] outrow6,
  output [15:0] outrow7,
  output [15:0] outrow8,
  output [15:0] outrow9,
  output [15:0] outrow10,
  output [15:0] outrow11,
  output [15:0] outrow12,
  output [15:0] outrow13,
  output [15:0] outrow14,
  output [15:0] outrow15
);

  wire clk_t, out1, out2, out3, out4, out5, out6, out7, out8, out9, out10, out11, out12, out13, out14, out15,
       out16, row_1_ex17, row_1_ex18, row_1_ex19, row_1_ex20, row_1_ex21, row_1_ex22, row_1_ex23, row_1_ex24,
       row_1_ex25, row_1_ex26, row_1_ex27, row_1_ex28, row_1_ex29, row_1_ex30, row_1_ex31, row_1_ex32,
       row_2_ex1, row_2_ex2, row_2_ex3, row_2_ex4, row_2_ex5, row_2_ex6, row_2_ex7, row_2_ex8, row_2_ex9,
       row_2_ex10, row_2_ex11, row_2_ex12, row_2_ex13, row_2_ex14, row_2_ex15, row_2_ex16, row_2_ex17,
       row_2_ex18, row_2_ex19, row_2_ex20, row_2_ex21, row_2_ex22, row_2_ex23, row_2_ex24, row_2_ex25,
       row_2_ex26, row_2_ex27, row_2_ex28, row_2_ex29, row_2_ex30, row_2_ex31, row_2_ex32, row_3_ex1,
       row_3_ex2, row_3_ex3, row_3_ex4, row_3_ex5, row_3_ex6, row_3_ex7, row_3_ex8, row_3_ex9, row_3_ex10,
       row_3_ex11, row_3_ex12, row_3_ex13, row_3_ex14, row_3_ex15, row_3_ex16, row_3_ex17, row_3_ex18,
       row_3_ex19, row_3_ex20, row_3_ex21, row_3_ex22, row_3_ex23, row_3_ex24, row_3_ex25, row_3_ex26,
       row_3_ex27, row_3_ex28, row_3_ex29, row_3_ex30, row_3_ex31, row_3_ex32, row_4_ex1, row_4_ex2,
       row_4_ex3, row_4_ex4, row_4_ex5, row_4_ex6, row_4_ex7, row_4_ex8, row_4_ex9, row_4_ex10, row_4_ex11,
       row_4_ex12, row_4_ex13, row_4_ex14, row_4_ex15, row_4_ex16, row_4_ex17, row_4_ex18, row_4_ex19,
       row_4_ex20, row_4_ex21, row_4_ex22, row_4_ex23, row_4_ex24, row_4_ex25, row_4_ex26, row_4_ex27,
       row_4_ex28, row_4_ex29, row_4_ex30, row_4_ex31, row_4_ex32, row_5_ex1, row_5_ex2, row_5_ex3,
       row_5_ex4, row_5_ex5, row_5_ex6, row_5_ex7, row_5_ex8, row_5_ex9, row_5_ex10, row_5_ex11, row_5_ex12,
       row_5_ex13, row_5_ex14, row_5_ex15, row_5_ex16, row_5_ex17, row_5_ex18, row_5_ex19, row_5_ex20,
       row_5_ex21, row_5_ex22, row_5_ex23, row_5_ex24, row_5_ex25, row_5_ex26, row_5_ex27, row_5_ex28,
       row_5_ex29, row_5_ex30, row_5_ex31, row_5_ex32, row_6_ex1, row_6_ex2, row_6_ex3, row_6_ex4, row_6_ex5,
       row_6_ex6, row_6_ex7, row_6_ex8, row_6_ex9, row_6_ex10, row_6_ex11, row_6_ex12, row_6_ex13,
       row_6_ex14, row_6_ex15, row_6_ex16, row_6_ex17, row_6_ex18, row_6_ex19, row_6_ex20, row_6_ex21,
       row_6_ex22, row_6_ex23, row_6_ex24, row_6_ex25, row_6_ex26, row_6_ex27, row_6_ex28, row_6_ex29,
       row_6_ex30, row_6_ex31, row_6_ex32, row_7_ex1, row_7_ex2, row_7_ex3, row_7_ex4, row_7_ex5, row_7_ex6,
       row_7_ex7, row_7_ex8, row_7_ex9, row_7_ex10, row_7_ex11, row_7_ex12, row_7_ex13, row_7_ex14,
       row_7_ex15, row_7_ex16, row_7_ex17, row_7_ex18, row_7_ex19, row_7_ex20, row_7_ex21, row_7_ex22,
       row_7_ex23, row_7_ex24, row_7_ex25, row_7_ex26, row_7_ex27, row_7_ex28, row_7_ex29, row_7_ex30,
       row_7_ex31, row_7_ex32, row_8_ex1, row_8_ex2, row_8_ex3, row_8_ex4, row_8_ex5, row_8_ex6, row_8_ex7,
       row_8_ex8, row_8_ex9, row_8_ex10, row_8_ex11, row_8_ex12, row_8_ex13, row_8_ex14, row_8_ex15,
       row_8_ex16, row_8_ex17, row_8_ex18, row_8_ex19, row_8_ex20, row_8_ex21, row_8_ex22, row_8_ex23,
       row_8_ex24, row_8_ex25, row_8_ex26, row_8_ex27, row_8_ex28, row_8_ex29, row_8_ex30, row_8_ex31,
       row_8_ex32, row_9_ex1, row_9_ex2, row_9_ex3, row_9_ex4, row_9_ex5, row_9_ex6, row_9_ex7, row_9_ex8,
       row_9_ex9, row_9_ex10, row_9_ex11, row_9_ex12, row_9_ex13, row_9_ex14, row_9_ex15, row_9_ex16,
       row_9_ex17, row_9_ex18, row_9_ex19, row_9_ex20, row_9_ex21, row_9_ex22, row_9_ex23, row_9_ex24,
       row_9_ex25, row_9_ex26, row_9_ex27, row_9_ex28, row_9_ex29, row_9_ex30, row_9_ex31, row_9_ex32,
       row_10_ex1, row_10_ex2, row_10_ex3, row_10_ex4, row_10_ex5, row_10_ex6, row_10_ex7, row_10_ex8,
       row_10_ex9, row_10_ex10, row_10_ex11, row_10_ex12, row_10_ex13, row_10_ex14, row_10_ex15, row_10_ex16,
       row_10_ex17, row_10_ex18, row_10_ex19, row_10_ex20, row_10_ex21, row_10_ex22, row_10_ex23,
       row_10_ex24, row_10_ex25, row_10_ex26, row_10_ex27, row_10_ex28, row_10_ex29, row_10_ex30,
       row_10_ex31, row_10_ex32, row_11_ex1, row_11_ex2, row_11_ex3, row_11_ex4, row_11_ex5, row_11_ex6,
       row_11_ex7, row_11_ex8, row_11_ex9, row_11_ex10, row_11_ex11, row_11_ex12, row_11_ex13, row_11_ex14,
       row_11_ex15, row_11_ex16, row_11_ex17, row_11_ex18, row_11_ex19, row_11_ex20, row_11_ex21,
       row_11_ex22, row_11_ex23, row_11_ex24, row_11_ex25, row_11_ex26, row_11_ex27, row_11_ex28,
       row_11_ex29, row_11_ex30, row_11_ex31, row_11_ex32, row_12_ex1, row_12_ex2, row_12_ex3, row_12_ex4,
       row_12_ex5, row_12_ex6, row_12_ex7, row_12_ex8, row_12_ex9, row_12_ex10, row_12_ex11, row_12_ex12,
       row_12_ex13, row_12_ex14, row_12_ex15, row_12_ex16, row_12_ex17, row_12_ex18, row_12_ex19,
       row_12_ex20, row_12_ex21, row_12_ex22, row_12_ex23, row_12_ex24, row_12_ex25, row_12_ex26,
       row_12_ex27, row_12_ex28, row_12_ex29, row_12_ex30, row_12_ex31, row_12_ex32, row_13_ex1, row_13_ex2,
       row_13_ex3, row_13_ex4, row_13_ex5, row_13_ex6, row_13_ex7, row_13_ex8, row_13_ex9, row_13_ex10,
       row_13_ex11, row_13_ex12, row_13_ex13, row_13_ex14, row_13_ex15, row_13_ex16, row_13_ex17,
       row_13_ex18, row_13_ex19, row_13_ex20, row_13_ex21, row_13_ex22, row_13_ex23, row_13_ex24,
       row_13_ex25, row_13_ex26, row_13_ex27, row_13_ex28, row_13_ex29, row_13_ex30, row_13_ex31,
       row_13_ex32, row_14_ex1, row_14_ex2, row_14_ex3, row_14_ex4, row_14_ex5, row_14_ex6, row_14_ex7,
       row_14_ex8, row_14_ex9, row_14_ex10, row_14_ex11, row_14_ex12, row_14_ex13, row_14_ex14, row_14_ex15,
       row_14_ex16, row_14_ex17, row_14_ex18, row_14_ex19, row_14_ex20, row_14_ex21, row_14_ex22,
       row_14_ex23, row_14_ex24, row_14_ex25, row_14_ex26, row_14_ex27, row_14_ex28, row_14_ex29,
       row_14_ex30, row_14_ex31, row_14_ex32, row_15_ex1, row_15_ex2, row_15_ex3, row_15_ex4, row_15_ex5,
       row_15_ex6, row_15_ex7, row_15_ex8, row_15_ex9, row_15_ex10, row_15_ex11, row_15_ex12, row_15_ex13,
       row_15_ex14, row_15_ex15, row_15_ex16, row_15_ex17, row_15_ex18, row_15_ex19, row_15_ex20,
       row_15_ex21, row_15_ex22, row_15_ex23, row_15_ex24, row_15_ex25, row_15_ex26, row_15_ex27,
       row_15_ex28, row_15_ex29, row_15_ex30, row_15_ex31, row_15_ex32, row_16_ex1, row_16_ex2, row_16_ex3,
       row_16_ex4, row_16_ex5, row_16_ex6, row_16_ex7, row_16_ex8, row_16_ex9, row_16_ex10, row_16_ex11,
       row_16_ex12, row_16_ex13, row_16_ex14, row_16_ex15, row_16_ex16, stop_t, t_ff_1_q, t_ff_3_q, t_ff_4_q,
       tun0, tun1, tun2, tun3, tun4, tun5, tun6, tun7, tun8, tun9, tun10, tun11, tun12, tun13, tun14, tun15,
       tun16, tun17, tun18, tun19, tun20, tun21, tun22, tun23, tun24, tun25, tun26, tun27, tun28, tun29,
       tun30, tun31;
  wire [3:0] adr_4bits;

  T_Flip_Flop t_ff_1 (.clk(clk), .T(clk), .Q(t_ff_1_q));  // open: Qn, preset, reset, en
  T_Flip_Flop t_ff_2 (.clk(stop), .T(stop), .Q(stop_t));  // open: Qn, preset, reset, en
  Clock clock_1 ();  // open: out
  T_Flip_Flop t_ff_3 (.clk(t_ff_1_q), .T(t_ff_1_q), .Q(t_ff_3_q));  // open: Qn, preset, reset, en
  T_Flip_Flop t_ff_4 (.clk(t_ff_3_q), .T(t_ff_3_q), .Q(t_ff_4_q));  // open: Qn, preset, reset, en
  and and_1 (clk_t, t_ff_4_q, ~stop_t);  // AND_Gate
  row row_1 (
    .clk(clk_t), .ex1(tun1), .nb1(tun0), .ex2(tun3), .nb2(tun2), .ex3(tun5), .nb3(tun4), .ex4(tun7),
    .nb4(tun6), .ex5(tun9), .nb5(tun8), .ex6(tun11), .nb6(tun10), .ex7(tun13), .nb7(tun12), .ex8(tun15),
    .nb8(tun14), .ex9(tun17), .nb9(tun16), .ex10(tun19), .nb10(tun18), .ex11(tun21), .nb11(tun20),
    .ex12(tun23), .nb12(tun22), .ex13(tun25), .nb13(tun24), .ex14(tun27), .nb14(tun26), .ex15(tun29),
    .nb15(tun28), .ex16(tun31), .nb16(tun30), .ex17(row_1_ex17), .nb17(row_2_ex1), .ex18(row_1_ex18),
    .nb18(row_2_ex2), .ex19(row_1_ex19), .nb19(row_2_ex3), .ex20(row_1_ex20), .nb20(row_2_ex4),
    .ex21(row_1_ex21), .nb21(row_2_ex5), .ex22(row_1_ex22), .nb22(row_2_ex6), .ex23(row_1_ex23),
    .nb23(row_2_ex7), .ex24(row_1_ex24), .nb24(row_2_ex8), .ex25(row_1_ex25), .nb25(row_2_ex9),
    .ex26(row_1_ex26), .nb26(row_2_ex10), .ex27(row_1_ex27), .nb27(row_2_ex11), .ex28(row_1_ex28),
    .nb28(row_2_ex12), .ex29(row_1_ex29), .nb29(row_2_ex13), .ex30(row_1_ex30), .nb30(row_2_ex14),
    .ex31(row_1_ex31), .nb31(row_2_ex15), .ex32(row_1_ex32), .nb32(row_2_ex16), .set(set0),
    .\output (outrow0), .cell_out(out1), .stop(stop_t), .adr(cell_x), .button(global_set), .restart(restart));
  row row_2 (
    .clk(clk_t), .ex1(row_2_ex1), .nb1(row_1_ex17), .ex2(row_2_ex2), .nb2(row_1_ex18), .ex3(row_2_ex3),
    .nb3(row_1_ex19), .ex4(row_2_ex4), .nb4(row_1_ex20), .ex5(row_2_ex5), .nb5(row_1_ex21), .ex6(row_2_ex6),
    .nb6(row_1_ex22), .ex7(row_2_ex7), .nb7(row_1_ex23), .ex8(row_2_ex8), .nb8(row_1_ex24), .ex9(row_2_ex9),
    .nb9(row_1_ex25), .ex10(row_2_ex10), .nb10(row_1_ex26), .ex11(row_2_ex11), .nb11(row_1_ex27),
    .ex12(row_2_ex12), .nb12(row_1_ex28), .ex13(row_2_ex13), .nb13(row_1_ex29), .ex14(row_2_ex14),
    .nb14(row_1_ex30), .ex15(row_2_ex15), .nb15(row_1_ex31), .ex16(row_2_ex16), .nb16(row_1_ex32),
    .ex17(row_2_ex17), .nb17(row_3_ex1), .ex18(row_2_ex18), .nb18(row_3_ex2), .ex19(row_2_ex19),
    .nb19(row_3_ex3), .ex20(row_2_ex20), .nb20(row_3_ex4), .ex21(row_2_ex21), .nb21(row_3_ex5),
    .ex22(row_2_ex22), .nb22(row_3_ex6), .ex23(row_2_ex23), .nb23(row_3_ex7), .ex24(row_2_ex24),
    .nb24(row_3_ex8), .ex25(row_2_ex25), .nb25(row_3_ex9), .ex26(row_2_ex26), .nb26(row_3_ex10),
    .ex27(row_2_ex27), .nb27(row_3_ex11), .ex28(row_2_ex28), .nb28(row_3_ex12), .ex29(row_2_ex29),
    .nb29(row_3_ex13), .ex30(row_2_ex30), .nb30(row_3_ex14), .ex31(row_2_ex31), .nb31(row_3_ex15),
    .ex32(row_2_ex32), .nb32(row_3_ex16), .set(set1), .\output (outrow1), .cell_out(out2), .stop(stop_t),
    .adr(cell_x), .button(global_set), .restart(restart));
  row row_3 (
    .clk(clk_t), .ex1(row_3_ex1), .nb1(row_2_ex17), .ex2(row_3_ex2), .nb2(row_2_ex18), .ex3(row_3_ex3),
    .nb3(row_2_ex19), .ex4(row_3_ex4), .nb4(row_2_ex20), .ex5(row_3_ex5), .nb5(row_2_ex21), .ex6(row_3_ex6),
    .nb6(row_2_ex22), .ex7(row_3_ex7), .nb7(row_2_ex23), .ex8(row_3_ex8), .nb8(row_2_ex24), .ex9(row_3_ex9),
    .nb9(row_2_ex25), .ex10(row_3_ex10), .nb10(row_2_ex26), .ex11(row_3_ex11), .nb11(row_2_ex27),
    .ex12(row_3_ex12), .nb12(row_2_ex28), .ex13(row_3_ex13), .nb13(row_2_ex29), .ex14(row_3_ex14),
    .nb14(row_2_ex30), .ex15(row_3_ex15), .nb15(row_2_ex31), .ex16(row_3_ex16), .nb16(row_2_ex32),
    .ex17(row_3_ex17), .nb17(row_4_ex1), .ex18(row_3_ex18), .nb18(row_4_ex2), .ex19(row_3_ex19),
    .nb19(row_4_ex3), .ex20(row_3_ex20), .nb20(row_4_ex4), .ex21(row_3_ex21), .nb21(row_4_ex5),
    .ex22(row_3_ex22), .nb22(row_4_ex6), .ex23(row_3_ex23), .nb23(row_4_ex7), .ex24(row_3_ex24),
    .nb24(row_4_ex8), .ex25(row_3_ex25), .nb25(row_4_ex9), .ex26(row_3_ex26), .nb26(row_4_ex10),
    .ex27(row_3_ex27), .nb27(row_4_ex11), .ex28(row_3_ex28), .nb28(row_4_ex12), .ex29(row_3_ex29),
    .nb29(row_4_ex13), .ex30(row_3_ex30), .nb30(row_4_ex14), .ex31(row_3_ex31), .nb31(row_4_ex15),
    .ex32(row_3_ex32), .nb32(row_4_ex16), .set(set2), .\output (outrow2), .cell_out(out3), .stop(stop_t),
    .adr(cell_x), .button(global_set), .restart(restart));
  row row_4 (
    .clk(clk_t), .ex1(row_4_ex1), .nb1(row_3_ex17), .ex2(row_4_ex2), .nb2(row_3_ex18), .ex3(row_4_ex3),
    .nb3(row_3_ex19), .ex4(row_4_ex4), .nb4(row_3_ex20), .ex5(row_4_ex5), .nb5(row_3_ex21), .ex6(row_4_ex6),
    .nb6(row_3_ex22), .ex7(row_4_ex7), .nb7(row_3_ex23), .ex8(row_4_ex8), .nb8(row_3_ex24), .ex9(row_4_ex9),
    .nb9(row_3_ex25), .ex10(row_4_ex10), .nb10(row_3_ex26), .ex11(row_4_ex11), .nb11(row_3_ex27),
    .ex12(row_4_ex12), .nb12(row_3_ex28), .ex13(row_4_ex13), .nb13(row_3_ex29), .ex14(row_4_ex14),
    .nb14(row_3_ex30), .ex15(row_4_ex15), .nb15(row_3_ex31), .ex16(row_4_ex16), .nb16(row_3_ex32),
    .ex17(row_4_ex17), .nb17(row_5_ex1), .ex18(row_4_ex18), .nb18(row_5_ex2), .ex19(row_4_ex19),
    .nb19(row_5_ex3), .ex20(row_4_ex20), .nb20(row_5_ex4), .ex21(row_4_ex21), .nb21(row_5_ex5),
    .ex22(row_4_ex22), .nb22(row_5_ex6), .ex23(row_4_ex23), .nb23(row_5_ex7), .ex24(row_4_ex24),
    .nb24(row_5_ex8), .ex25(row_4_ex25), .nb25(row_5_ex9), .ex26(row_4_ex26), .nb26(row_5_ex10),
    .ex27(row_4_ex27), .nb27(row_5_ex11), .ex28(row_4_ex28), .nb28(row_5_ex12), .ex29(row_4_ex29),
    .nb29(row_5_ex13), .ex30(row_4_ex30), .nb30(row_5_ex14), .ex31(row_4_ex31), .nb31(row_5_ex15),
    .ex32(row_4_ex32), .nb32(row_5_ex16), .set(set3), .\output (outrow3), .cell_out(out4), .stop(stop_t),
    .adr(cell_x), .button(global_set), .restart(restart));
  row row_5 (
    .clk(clk_t), .ex1(row_5_ex1), .nb1(row_4_ex17), .ex2(row_5_ex2), .nb2(row_4_ex18), .ex3(row_5_ex3),
    .nb3(row_4_ex19), .ex4(row_5_ex4), .nb4(row_4_ex20), .ex5(row_5_ex5), .nb5(row_4_ex21), .ex6(row_5_ex6),
    .nb6(row_4_ex22), .ex7(row_5_ex7), .nb7(row_4_ex23), .ex8(row_5_ex8), .nb8(row_4_ex24), .ex9(row_5_ex9),
    .nb9(row_4_ex25), .ex10(row_5_ex10), .nb10(row_4_ex26), .ex11(row_5_ex11), .nb11(row_4_ex27),
    .ex12(row_5_ex12), .nb12(row_4_ex28), .ex13(row_5_ex13), .nb13(row_4_ex29), .ex14(row_5_ex14),
    .nb14(row_4_ex30), .ex15(row_5_ex15), .nb15(row_4_ex31), .ex16(row_5_ex16), .nb16(row_4_ex32),
    .ex17(row_5_ex17), .nb17(row_6_ex1), .ex18(row_5_ex18), .nb18(row_6_ex2), .ex19(row_5_ex19),
    .nb19(row_6_ex3), .ex20(row_5_ex20), .nb20(row_6_ex4), .ex21(row_5_ex21), .nb21(row_6_ex5),
    .ex22(row_5_ex22), .nb22(row_6_ex6), .ex23(row_5_ex23), .nb23(row_6_ex7), .ex24(row_5_ex24),
    .nb24(row_6_ex8), .ex25(row_5_ex25), .nb25(row_6_ex9), .ex26(row_5_ex26), .nb26(row_6_ex10),
    .ex27(row_5_ex27), .nb27(row_6_ex11), .ex28(row_5_ex28), .nb28(row_6_ex12), .ex29(row_5_ex29),
    .nb29(row_6_ex13), .ex30(row_5_ex30), .nb30(row_6_ex14), .ex31(row_5_ex31), .nb31(row_6_ex15),
    .ex32(row_5_ex32), .nb32(row_6_ex16), .set(set4), .\output (outrow4), .cell_out(out5), .stop(stop_t),
    .adr(cell_x), .button(global_set), .restart(restart));
  row row_6 (
    .clk(clk_t), .ex1(row_6_ex1), .nb1(row_5_ex17), .ex2(row_6_ex2), .nb2(row_5_ex18), .ex3(row_6_ex3),
    .nb3(row_5_ex19), .ex4(row_6_ex4), .nb4(row_5_ex20), .ex5(row_6_ex5), .nb5(row_5_ex21), .ex6(row_6_ex6),
    .nb6(row_5_ex22), .ex7(row_6_ex7), .nb7(row_5_ex23), .ex8(row_6_ex8), .nb8(row_5_ex24), .ex9(row_6_ex9),
    .nb9(row_5_ex25), .ex10(row_6_ex10), .nb10(row_5_ex26), .ex11(row_6_ex11), .nb11(row_5_ex27),
    .ex12(row_6_ex12), .nb12(row_5_ex28), .ex13(row_6_ex13), .nb13(row_5_ex29), .ex14(row_6_ex14),
    .nb14(row_5_ex30), .ex15(row_6_ex15), .nb15(row_5_ex31), .ex16(row_6_ex16), .nb16(row_5_ex32),
    .ex17(row_6_ex17), .nb17(row_7_ex1), .ex18(row_6_ex18), .nb18(row_7_ex2), .ex19(row_6_ex19),
    .nb19(row_7_ex3), .ex20(row_6_ex20), .nb20(row_7_ex4), .ex21(row_6_ex21), .nb21(row_7_ex5),
    .ex22(row_6_ex22), .nb22(row_7_ex6), .ex23(row_6_ex23), .nb23(row_7_ex7), .ex24(row_6_ex24),
    .nb24(row_7_ex8), .ex25(row_6_ex25), .nb25(row_7_ex9), .ex26(row_6_ex26), .nb26(row_7_ex10),
    .ex27(row_6_ex27), .nb27(row_7_ex11), .ex28(row_6_ex28), .nb28(row_7_ex12), .ex29(row_6_ex29),
    .nb29(row_7_ex13), .ex30(row_6_ex30), .nb30(row_7_ex14), .ex31(row_6_ex31), .nb31(row_7_ex15),
    .ex32(row_6_ex32), .nb32(row_7_ex16), .set(set5), .\output (outrow5), .cell_out(out6), .stop(stop_t),
    .adr(cell_x), .button(global_set), .restart(restart));
  row row_7 (
    .clk(clk_t), .ex1(row_7_ex1), .nb1(row_6_ex17), .ex2(row_7_ex2), .nb2(row_6_ex18), .ex3(row_7_ex3),
    .nb3(row_6_ex19), .ex4(row_7_ex4), .nb4(row_6_ex20), .ex5(row_7_ex5), .nb5(row_6_ex21), .ex6(row_7_ex6),
    .nb6(row_6_ex22), .ex7(row_7_ex7), .nb7(row_6_ex23), .ex8(row_7_ex8), .nb8(row_6_ex24), .ex9(row_7_ex9),
    .nb9(row_6_ex25), .ex10(row_7_ex10), .nb10(row_6_ex26), .ex11(row_7_ex11), .nb11(row_6_ex27),
    .ex12(row_7_ex12), .nb12(row_6_ex28), .ex13(row_7_ex13), .nb13(row_6_ex29), .ex14(row_7_ex14),
    .nb14(row_6_ex30), .ex15(row_7_ex15), .nb15(row_6_ex31), .ex16(row_7_ex16), .nb16(row_6_ex32),
    .ex17(row_7_ex17), .nb17(row_8_ex1), .ex18(row_7_ex18), .nb18(row_8_ex2), .ex19(row_7_ex19),
    .nb19(row_8_ex3), .ex20(row_7_ex20), .nb20(row_8_ex4), .ex21(row_7_ex21), .nb21(row_8_ex5),
    .ex22(row_7_ex22), .nb22(row_8_ex6), .ex23(row_7_ex23), .nb23(row_8_ex7), .ex24(row_7_ex24),
    .nb24(row_8_ex8), .ex25(row_7_ex25), .nb25(row_8_ex9), .ex26(row_7_ex26), .nb26(row_8_ex10),
    .ex27(row_7_ex27), .nb27(row_8_ex11), .ex28(row_7_ex28), .nb28(row_8_ex12), .ex29(row_7_ex29),
    .nb29(row_8_ex13), .ex30(row_7_ex30), .nb30(row_8_ex14), .ex31(row_7_ex31), .nb31(row_8_ex15),
    .ex32(row_7_ex32), .nb32(row_8_ex16), .set(set6), .\output (outrow6), .cell_out(out7), .stop(stop_t),
    .adr(cell_x), .button(global_set), .restart(restart));
  row row_8 (
    .clk(clk_t), .ex1(row_8_ex1), .nb1(row_7_ex17), .ex2(row_8_ex2), .nb2(row_7_ex18), .ex3(row_8_ex3),
    .nb3(row_7_ex19), .ex4(row_8_ex4), .nb4(row_7_ex20), .ex5(row_8_ex5), .nb5(row_7_ex21), .ex6(row_8_ex6),
    .nb6(row_7_ex22), .ex7(row_8_ex7), .nb7(row_7_ex23), .ex8(row_8_ex8), .nb8(row_7_ex24), .ex9(row_8_ex9),
    .nb9(row_7_ex25), .ex10(row_8_ex10), .nb10(row_7_ex26), .ex11(row_8_ex11), .nb11(row_7_ex27),
    .ex12(row_8_ex12), .nb12(row_7_ex28), .ex13(row_8_ex13), .nb13(row_7_ex29), .ex14(row_8_ex14),
    .nb14(row_7_ex30), .ex15(row_8_ex15), .nb15(row_7_ex31), .ex16(row_8_ex16), .nb16(row_7_ex32),
    .ex17(row_8_ex17), .nb17(row_9_ex1), .ex18(row_8_ex18), .nb18(row_9_ex2), .ex19(row_8_ex19),
    .nb19(row_9_ex3), .ex20(row_8_ex20), .nb20(row_9_ex4), .ex21(row_8_ex21), .nb21(row_9_ex5),
    .ex22(row_8_ex22), .nb22(row_9_ex6), .ex23(row_8_ex23), .nb23(row_9_ex7), .ex24(row_8_ex24),
    .nb24(row_9_ex8), .ex25(row_8_ex25), .nb25(row_9_ex9), .ex26(row_8_ex26), .nb26(row_9_ex10),
    .ex27(row_8_ex27), .nb27(row_9_ex11), .ex28(row_8_ex28), .nb28(row_9_ex12), .ex29(row_8_ex29),
    .nb29(row_9_ex13), .ex30(row_8_ex30), .nb30(row_9_ex14), .ex31(row_8_ex31), .nb31(row_9_ex15),
    .ex32(row_8_ex32), .nb32(row_9_ex16), .set(set7), .\output (outrow7), .cell_out(out8), .stop(stop_t),
    .adr(cell_x), .button(global_set), .restart(restart));
  row row_9 (
    .clk(clk_t), .ex1(row_9_ex1), .nb1(row_8_ex17), .ex2(row_9_ex2), .nb2(row_8_ex18), .ex3(row_9_ex3),
    .nb3(row_8_ex19), .ex4(row_9_ex4), .nb4(row_8_ex20), .ex5(row_9_ex5), .nb5(row_8_ex21), .ex6(row_9_ex6),
    .nb6(row_8_ex22), .ex7(row_9_ex7), .nb7(row_8_ex23), .ex8(row_9_ex8), .nb8(row_8_ex24), .ex9(row_9_ex9),
    .nb9(row_8_ex25), .ex10(row_9_ex10), .nb10(row_8_ex26), .ex11(row_9_ex11), .nb11(row_8_ex27),
    .ex12(row_9_ex12), .nb12(row_8_ex28), .ex13(row_9_ex13), .nb13(row_8_ex29), .ex14(row_9_ex14),
    .nb14(row_8_ex30), .ex15(row_9_ex15), .nb15(row_8_ex31), .ex16(row_9_ex16), .nb16(row_8_ex32),
    .ex17(row_9_ex17), .nb17(row_10_ex1), .ex18(row_9_ex18), .nb18(row_10_ex2), .ex19(row_9_ex19),
    .nb19(row_10_ex3), .ex20(row_9_ex20), .nb20(row_10_ex4), .ex21(row_9_ex21), .nb21(row_10_ex5),
    .ex22(row_9_ex22), .nb22(row_10_ex6), .ex23(row_9_ex23), .nb23(row_10_ex7), .ex24(row_9_ex24),
    .nb24(row_10_ex8), .ex25(row_9_ex25), .nb25(row_10_ex9), .ex26(row_9_ex26), .nb26(row_10_ex10),
    .ex27(row_9_ex27), .nb27(row_10_ex11), .ex28(row_9_ex28), .nb28(row_10_ex12), .ex29(row_9_ex29),
    .nb29(row_10_ex13), .ex30(row_9_ex30), .nb30(row_10_ex14), .ex31(row_9_ex31), .nb31(row_10_ex15),
    .ex32(row_9_ex32), .nb32(row_10_ex16), .set(set8), .\output (outrow8), .cell_out(out9), .stop(stop_t),
    .adr(cell_x), .button(global_set), .restart(restart));
  row row_10 (
    .clk(clk_t), .ex1(row_10_ex1), .nb1(row_9_ex17), .ex2(row_10_ex2), .nb2(row_9_ex18), .ex3(row_10_ex3),
    .nb3(row_9_ex19), .ex4(row_10_ex4), .nb4(row_9_ex20), .ex5(row_10_ex5), .nb5(row_9_ex21),
    .ex6(row_10_ex6), .nb6(row_9_ex22), .ex7(row_10_ex7), .nb7(row_9_ex23), .ex8(row_10_ex8),
    .nb8(row_9_ex24), .ex9(row_10_ex9), .nb9(row_9_ex25), .ex10(row_10_ex10), .nb10(row_9_ex26),
    .ex11(row_10_ex11), .nb11(row_9_ex27), .ex12(row_10_ex12), .nb12(row_9_ex28), .ex13(row_10_ex13),
    .nb13(row_9_ex29), .ex14(row_10_ex14), .nb14(row_9_ex30), .ex15(row_10_ex15), .nb15(row_9_ex31),
    .ex16(row_10_ex16), .nb16(row_9_ex32), .ex17(row_10_ex17), .nb17(row_11_ex1), .ex18(row_10_ex18),
    .nb18(row_11_ex2), .ex19(row_10_ex19), .nb19(row_11_ex3), .ex20(row_10_ex20), .nb20(row_11_ex4),
    .ex21(row_10_ex21), .nb21(row_11_ex5), .ex22(row_10_ex22), .nb22(row_11_ex6), .ex23(row_10_ex23),
    .nb23(row_11_ex7), .ex24(row_10_ex24), .nb24(row_11_ex8), .ex25(row_10_ex25), .nb25(row_11_ex9),
    .ex26(row_10_ex26), .nb26(row_11_ex10), .ex27(row_10_ex27), .nb27(row_11_ex11), .ex28(row_10_ex28),
    .nb28(row_11_ex12), .ex29(row_10_ex29), .nb29(row_11_ex13), .ex30(row_10_ex30), .nb30(row_11_ex14),
    .ex31(row_10_ex31), .nb31(row_11_ex15), .ex32(row_10_ex32), .nb32(row_11_ex16), .set(set9),
    .\output (outrow9), .cell_out(out10), .stop(stop_t), .adr(cell_x), .button(global_set), .restart(restart));
  row row_11 (
    .clk(clk_t), .ex1(row_11_ex1), .nb1(row_10_ex17), .ex2(row_11_ex2), .nb2(row_10_ex18), .ex3(row_11_ex3),
    .nb3(row_10_ex19), .ex4(row_11_ex4), .nb4(row_10_ex20), .ex5(row_11_ex5), .nb5(row_10_ex21),
    .ex6(row_11_ex6), .nb6(row_10_ex22), .ex7(row_11_ex7), .nb7(row_10_ex23), .ex8(row_11_ex8),
    .nb8(row_10_ex24), .ex9(row_11_ex9), .nb9(row_10_ex25), .ex10(row_11_ex10), .nb10(row_10_ex26),
    .ex11(row_11_ex11), .nb11(row_10_ex27), .ex12(row_11_ex12), .nb12(row_10_ex28), .ex13(row_11_ex13),
    .nb13(row_10_ex29), .ex14(row_11_ex14), .nb14(row_10_ex30), .ex15(row_11_ex15), .nb15(row_10_ex31),
    .ex16(row_11_ex16), .nb16(row_10_ex32), .ex17(row_11_ex17), .nb17(row_12_ex1), .ex18(row_11_ex18),
    .nb18(row_12_ex2), .ex19(row_11_ex19), .nb19(row_12_ex3), .ex20(row_11_ex20), .nb20(row_12_ex4),
    .ex21(row_11_ex21), .nb21(row_12_ex5), .ex22(row_11_ex22), .nb22(row_12_ex6), .ex23(row_11_ex23),
    .nb23(row_12_ex7), .ex24(row_11_ex24), .nb24(row_12_ex8), .ex25(row_11_ex25), .nb25(row_12_ex9),
    .ex26(row_11_ex26), .nb26(row_12_ex10), .ex27(row_11_ex27), .nb27(row_12_ex11), .ex28(row_11_ex28),
    .nb28(row_12_ex12), .ex29(row_11_ex29), .nb29(row_12_ex13), .ex30(row_11_ex30), .nb30(row_12_ex14),
    .ex31(row_11_ex31), .nb31(row_12_ex15), .ex32(row_11_ex32), .nb32(row_12_ex16), .set(set10),
    .\output (outrow10), .cell_out(out11), .stop(stop_t), .adr(cell_x), .button(global_set), .restart(restart));
  row row_12 (
    .clk(clk_t), .ex1(row_12_ex1), .nb1(row_11_ex17), .ex2(row_12_ex2), .nb2(row_11_ex18), .ex3(row_12_ex3),
    .nb3(row_11_ex19), .ex4(row_12_ex4), .nb4(row_11_ex20), .ex5(row_12_ex5), .nb5(row_11_ex21),
    .ex6(row_12_ex6), .nb6(row_11_ex22), .ex7(row_12_ex7), .nb7(row_11_ex23), .ex8(row_12_ex8),
    .nb8(row_11_ex24), .ex9(row_12_ex9), .nb9(row_11_ex25), .ex10(row_12_ex10), .nb10(row_11_ex26),
    .ex11(row_12_ex11), .nb11(row_11_ex27), .ex12(row_12_ex12), .nb12(row_11_ex28), .ex13(row_12_ex13),
    .nb13(row_11_ex29), .ex14(row_12_ex14), .nb14(row_11_ex30), .ex15(row_12_ex15), .nb15(row_11_ex31),
    .ex16(row_12_ex16), .nb16(row_11_ex32), .ex17(row_12_ex17), .nb17(row_13_ex1), .ex18(row_12_ex18),
    .nb18(row_13_ex2), .ex19(row_12_ex19), .nb19(row_13_ex3), .ex20(row_12_ex20), .nb20(row_13_ex4),
    .ex21(row_12_ex21), .nb21(row_13_ex5), .ex22(row_12_ex22), .nb22(row_13_ex6), .ex23(row_12_ex23),
    .nb23(row_13_ex7), .ex24(row_12_ex24), .nb24(row_13_ex8), .ex25(row_12_ex25), .nb25(row_13_ex9),
    .ex26(row_12_ex26), .nb26(row_13_ex10), .ex27(row_12_ex27), .nb27(row_13_ex11), .ex28(row_12_ex28),
    .nb28(row_13_ex12), .ex29(row_12_ex29), .nb29(row_13_ex13), .ex30(row_12_ex30), .nb30(row_13_ex14),
    .ex31(row_12_ex31), .nb31(row_13_ex15), .ex32(row_12_ex32), .nb32(row_13_ex16), .set(set11),
    .\output (outrow11), .cell_out(out12), .stop(stop_t), .adr(cell_x), .button(global_set), .restart(restart));
  row row_13 (
    .clk(clk_t), .ex1(row_13_ex1), .nb1(row_12_ex17), .ex2(row_13_ex2), .nb2(row_12_ex18), .ex3(row_13_ex3),
    .nb3(row_12_ex19), .ex4(row_13_ex4), .nb4(row_12_ex20), .ex5(row_13_ex5), .nb5(row_12_ex21),
    .ex6(row_13_ex6), .nb6(row_12_ex22), .ex7(row_13_ex7), .nb7(row_12_ex23), .ex8(row_13_ex8),
    .nb8(row_12_ex24), .ex9(row_13_ex9), .nb9(row_12_ex25), .ex10(row_13_ex10), .nb10(row_12_ex26),
    .ex11(row_13_ex11), .nb11(row_12_ex27), .ex12(row_13_ex12), .nb12(row_12_ex28), .ex13(row_13_ex13),
    .nb13(row_12_ex29), .ex14(row_13_ex14), .nb14(row_12_ex30), .ex15(row_13_ex15), .nb15(row_12_ex31),
    .ex16(row_13_ex16), .nb16(row_12_ex32), .ex17(row_13_ex17), .nb17(row_14_ex1), .ex18(row_13_ex18),
    .nb18(row_14_ex2), .ex19(row_13_ex19), .nb19(row_14_ex3), .ex20(row_13_ex20), .nb20(row_14_ex4),
    .ex21(row_13_ex21), .nb21(row_14_ex5), .ex22(row_13_ex22), .nb22(row_14_ex6), .ex23(row_13_ex23),
    .nb23(row_14_ex7), .ex24(row_13_ex24), .nb24(row_14_ex8), .ex25(row_13_ex25), .nb25(row_14_ex9),
    .ex26(row_13_ex26), .nb26(row_14_ex10), .ex27(row_13_ex27), .nb27(row_14_ex11), .ex28(row_13_ex28),
    .nb28(row_14_ex12), .ex29(row_13_ex29), .nb29(row_14_ex13), .ex30(row_13_ex30), .nb30(row_14_ex14),
    .ex31(row_13_ex31), .nb31(row_14_ex15), .ex32(row_13_ex32), .nb32(row_14_ex16), .set(set12),
    .\output (outrow12), .cell_out(out13), .stop(stop_t), .adr(cell_x), .button(global_set), .restart(restart));
  row row_14 (
    .clk(clk_t), .ex1(row_14_ex1), .nb1(row_13_ex17), .ex2(row_14_ex2), .nb2(row_13_ex18), .ex3(row_14_ex3),
    .nb3(row_13_ex19), .ex4(row_14_ex4), .nb4(row_13_ex20), .ex5(row_14_ex5), .nb5(row_13_ex21),
    .ex6(row_14_ex6), .nb6(row_13_ex22), .ex7(row_14_ex7), .nb7(row_13_ex23), .ex8(row_14_ex8),
    .nb8(row_13_ex24), .ex9(row_14_ex9), .nb9(row_13_ex25), .ex10(row_14_ex10), .nb10(row_13_ex26),
    .ex11(row_14_ex11), .nb11(row_13_ex27), .ex12(row_14_ex12), .nb12(row_13_ex28), .ex13(row_14_ex13),
    .nb13(row_13_ex29), .ex14(row_14_ex14), .nb14(row_13_ex30), .ex15(row_14_ex15), .nb15(row_13_ex31),
    .ex16(row_14_ex16), .nb16(row_13_ex32), .ex17(row_14_ex17), .nb17(row_15_ex1), .ex18(row_14_ex18),
    .nb18(row_15_ex2), .ex19(row_14_ex19), .nb19(row_15_ex3), .ex20(row_14_ex20), .nb20(row_15_ex4),
    .ex21(row_14_ex21), .nb21(row_15_ex5), .ex22(row_14_ex22), .nb22(row_15_ex6), .ex23(row_14_ex23),
    .nb23(row_15_ex7), .ex24(row_14_ex24), .nb24(row_15_ex8), .ex25(row_14_ex25), .nb25(row_15_ex9),
    .ex26(row_14_ex26), .nb26(row_15_ex10), .ex27(row_14_ex27), .nb27(row_15_ex11), .ex28(row_14_ex28),
    .nb28(row_15_ex12), .ex29(row_14_ex29), .nb29(row_15_ex13), .ex30(row_14_ex30), .nb30(row_15_ex14),
    .ex31(row_14_ex31), .nb31(row_15_ex15), .ex32(row_14_ex32), .nb32(row_15_ex16), .set(set13),
    .\output (outrow13), .cell_out(out14), .stop(stop_t), .adr(cell_x), .button(global_set), .restart(restart));
  row row_15 (
    .clk(clk_t), .ex1(row_15_ex1), .nb1(row_14_ex17), .ex2(row_15_ex2), .nb2(row_14_ex18), .ex3(row_15_ex3),
    .nb3(row_14_ex19), .ex4(row_15_ex4), .nb4(row_14_ex20), .ex5(row_15_ex5), .nb5(row_14_ex21),
    .ex6(row_15_ex6), .nb6(row_14_ex22), .ex7(row_15_ex7), .nb7(row_14_ex23), .ex8(row_15_ex8),
    .nb8(row_14_ex24), .ex9(row_15_ex9), .nb9(row_14_ex25), .ex10(row_15_ex10), .nb10(row_14_ex26),
    .ex11(row_15_ex11), .nb11(row_14_ex27), .ex12(row_15_ex12), .nb12(row_14_ex28), .ex13(row_15_ex13),
    .nb13(row_14_ex29), .ex14(row_15_ex14), .nb14(row_14_ex30), .ex15(row_15_ex15), .nb15(row_14_ex31),
    .ex16(row_15_ex16), .nb16(row_14_ex32), .ex17(row_15_ex17), .nb17(row_16_ex1), .ex18(row_15_ex18),
    .nb18(row_16_ex2), .ex19(row_15_ex19), .nb19(row_16_ex3), .ex20(row_15_ex20), .nb20(row_16_ex4),
    .ex21(row_15_ex21), .nb21(row_16_ex5), .ex22(row_15_ex22), .nb22(row_16_ex6), .ex23(row_15_ex23),
    .nb23(row_16_ex7), .ex24(row_15_ex24), .nb24(row_16_ex8), .ex25(row_15_ex25), .nb25(row_16_ex9),
    .ex26(row_15_ex26), .nb26(row_16_ex10), .ex27(row_15_ex27), .nb27(row_16_ex11), .ex28(row_15_ex28),
    .nb28(row_16_ex12), .ex29(row_15_ex29), .nb29(row_16_ex13), .ex30(row_15_ex30), .nb30(row_16_ex14),
    .ex31(row_15_ex31), .nb31(row_16_ex15), .ex32(row_15_ex32), .nb32(row_16_ex16), .set(set14),
    .\output (outrow14), .cell_out(out15), .stop(stop_t), .adr(cell_x), .button(global_set), .restart(restart));
  row row_16 (
    .clk(clk_t), .ex1(row_16_ex1), .nb1(row_15_ex17), .ex2(row_16_ex2), .nb2(row_15_ex18), .ex3(row_16_ex3),
    .nb3(row_15_ex19), .ex4(row_16_ex4), .nb4(row_15_ex20), .ex5(row_16_ex5), .nb5(row_15_ex21),
    .ex6(row_16_ex6), .nb6(row_15_ex22), .ex7(row_16_ex7), .nb7(row_15_ex23), .ex8(row_16_ex8),
    .nb8(row_15_ex24), .ex9(row_16_ex9), .nb9(row_15_ex25), .ex10(row_16_ex10), .nb10(row_15_ex26),
    .ex11(row_16_ex11), .nb11(row_15_ex27), .ex12(row_16_ex12), .nb12(row_15_ex28), .ex13(row_16_ex13),
    .nb13(row_15_ex29), .ex14(row_16_ex14), .nb14(row_15_ex30), .ex15(row_16_ex15), .nb15(row_15_ex31),
    .ex16(row_16_ex16), .nb16(row_15_ex32), .ex17(tun0), .nb17(tun1), .ex18(tun2), .nb18(tun3), .ex19(tun4),
    .nb19(tun5), .ex20(tun6), .nb20(tun7), .ex21(tun8), .nb21(tun9), .ex22(tun10), .nb22(tun11),
    .ex23(tun12), .nb23(tun13), .ex24(tun14), .nb24(tun15), .ex25(tun16), .nb25(tun17), .ex26(tun18),
    .nb26(tun19), .ex27(tun20), .nb27(tun21), .ex28(tun22), .nb28(tun23), .ex29(tun24), .nb29(tun25),
    .ex30(tun26), .nb30(tun27), .ex31(tun28), .nb31(tun29), .ex32(tun30), .nb32(tun31), .set(set15),
    .\output (outrow15), .cell_out(out16), .stop(stop_t), .adr(cell_x), .button(global_set), .restart(restart));
  Multiplexer #(.select(4), .enable("false")) multiplexer_1 (
    .in0(out1), .in1(out2), .in2(out3), .in3(out4), .in4(out5), .in5(out6), .in6(out7), .in7(out8),
    .in8(out9), .in9(out10), .in10(out11), .in11(out12), .in12(out13), .in13(out14), .in14(out15),
    .in15(out16), .out(cell_out), .sel(adr_4bits));

  // Other names for the same wires on the sheet: adr[7:0] = cell_x; rstrt = restart; set_gl = global_set
endmodule

module bcd (
  input  [7:0] \input ,
  output [3:0] big_digit,
  output [3:0] small_digit
);

  wire comparator_1_eq, comparator_1_gt;
  wire [3:0] subtractor_1_out;

  Comparator #(.width(4), .mode("unsigned")) comparator_1 (
    .a(\input [3:0]), .b(4'b1010), .gt(comparator_1_gt), .eq(comparator_1_eq));  // open: lt
  or or_1 (big_digit[0], comparator_1_gt, comparator_1_eq);
  Subtractor #(.width(4)) subtractor_1 (.a(\input [3:0]), .b(4'b1010), .out(subtractor_1_out));  // open: bin, bout
  Multiplexer #(.width(4), .enable("false")) multiplexer_1 (
    .in0(\input [3:0]), .in1(subtractor_1_out), .out(small_digit), .sel(big_digit[0]));

  assign big_digit[3:1] = 3'b000;
endmodule

module keyboard (
  input  sel,
  input  [4:0] I_O_adr,
  input  glider,
  input  lwss,
  input  explosion,
  output [7:0] I_O_dat
);

  wire and_1_out, and_2_out, not_1_out, not_2_out, transistor_1_out;
  wire [7:0] controlled_buffer_1_out, register_1_q;

  Transistor #(.\type ("n")) transistor_1 (.in(1'b0), .out(transistor_1_out), .gate(glider));
  assign controlled_buffer_1_out = glider ? 8'h1 : 8'bz;  // Controlled_Buffer controlled_buffer_1
  Transistor #(.\type ("n")) transistor_2 (.in(1'b0), .out(transistor_1_out), .gate(lwss));
  assign controlled_buffer_1_out = lwss ? 8'h2 : 8'bz;  // Controlled_Buffer controlled_buffer_2
  Transistor #(.\type ("n")) transistor_3 (.in(1'b0), .out(transistor_1_out), .gate(explosion));
  assign controlled_buffer_1_out = explosion ? 8'h3 : 8'bz;  // Controlled_Buffer controlled_buffer_3
  Pull_Resistor #(.pull(1)) pull_resistor_1 (.node(transistor_1_out));
  not not_1 (not_1_out, transistor_1_out);
  not not_2 (not_2_out, not_1_out);
  Register #(.trigger("high")) register_1 (
    .D(controlled_buffer_1_out), .Q(register_1_q), .clk(not_2_out), .clr(and_1_out));  // open: en
  and and_1 (and_1_out, ~sel, and_2_out);  // AND_Gate
  and and_2 (and_2_out, I_O_adr[4], ~I_O_adr[3], I_O_adr[2], I_O_adr[1], I_O_adr[0], sel);  // AND_Gate
  assign I_O_dat = and_2_out ? register_1_q : 8'bz;  // Controlled_Buffer controlled_buffer_4
endmodule

module beauty (
);

  wire button_1_out, button_2_out, button_3_out, button_4_out, button_5_out, button_6_out;
  wire [3:0] joystick_1_x, joystick_1_y, main_1_big_x, main_1_big_y, main_1_small_x, main_1_small_y;
  wire [15:0] main_1_outrow0, main_1_outrow1, main_1_outrow2, main_1_outrow3, main_1_outrow4, main_1_outrow5,
       main_1_outrow6, main_1_outrow7, main_1_outrow8, main_1_outrow9, main_1_outrow10, main_1_outrow11,
       main_1_outrow12, main_1_outrow13, main_1_outrow14, main_1_outrow15;

  Button button_1 (.out(button_1_out));
  Button button_2 (.out(button_2_out));
  Button button_3 (.out(button_3_out));
  Joystick joystick_1 (.x(joystick_1_x), .y(joystick_1_y));
  Hex_Digit_Display hex_digit_display_1 (.value(main_1_big_y));  // open: dp
  Hex_Digit_Display hex_digit_display_2 (.value(main_1_small_y));  // open: dp
  Button button_4 (.out(button_4_out));
  Button button_5 (.out(button_5_out));
  Hex_Digit_Display hex_digit_display_3 (.value(main_1_big_x));  // open: dp
  Button button_6 (.out(button_6_out));
  DotMatrix #(.inputtype("row"), .matrixcols(16), .matrixrows(16)) dotmatrix_1 (
    .row0(main_1_outrow0), .row1(main_1_outrow1), .row2(main_1_outrow2), .row3(main_1_outrow3),
    .row4(main_1_outrow4), .row5(main_1_outrow5), .row6(main_1_outrow6), .row7(main_1_outrow7),
    .row8(main_1_outrow8), .row9(main_1_outrow9), .row10(main_1_outrow10), .row11(main_1_outrow11),
    .row12(main_1_outrow12), .row13(main_1_outrow13), .row14(main_1_outrow14), .row15(main_1_outrow15));
  Hex_Digit_Display hex_digit_display_4 (.value(main_1_small_x));  // open: dp
  main main_1 (
    .joystick_x(joystick_1_x), .joystick_y(joystick_1_y), .set(button_4_out), .stop(button_5_out),
    .restart(button_6_out), .glider(button_1_out), .lwss(button_2_out), .explosion(button_3_out),
    .outrow0(main_1_outrow0), .outrow1(main_1_outrow1), .outrow2(main_1_outrow2), .outrow3(main_1_outrow3),
    .outrow4(main_1_outrow4), .outrow5(main_1_outrow5), .outrow6(main_1_outrow6), .outrow7(main_1_outrow7),
    .outrow8(main_1_outrow8), .outrow9(main_1_outrow9), .outrow10(main_1_outrow10),
    .outrow11(main_1_outrow11), .outrow12(main_1_outrow12), .outrow13(main_1_outrow13),
    .outrow14(main_1_outrow14), .outrow15(main_1_outrow15), .big_y(main_1_big_y), .small_y(main_1_small_y),
    .small_x(main_1_small_x), .big_x(main_1_big_x));

  // Notes on the sheet:
  //   glider
  //   lwss
  //   x-pentomino
  //   set
  //   stop
  //   restart
endmodule
